# Fritzing sketch Untitled Sketch (saved by Fritzing 0.9.3b)
circuit board: 8.46667cm x 5.64444cm
breadboards: 2

parts:
  Disp1 = LBT2088AH [part_number=LBT2088AH]
  元件1 = Arduino Nano (Rev3.0) (ICSP)
  U1 = 74HC595 [package="DIP16 [THT]"]
  U2 = 74HC595 [package="DIP16 [THT]"]
  R2 = Resistor [tolerance=±5% resistance=220 package=THT]
  R3 = Resistor [tolerance=±5% resistance=220 package=THT]
  R4 = Resistor [tolerance=±5% resistance=220 package=THT]
  R5 = Resistor [tolerance=±5% resistance=220 package=THT]
  R6 = Resistor [tolerance=±5% resistance=220 package=THT]
  R7 = Resistor [tolerance=±5% resistance=220 package=THT]
  R8 = Resistor [tolerance=±5% resistance=220 package=THT]
  R9 = Resistor [tolerance=±5% resistance=220 package=THT]

nets:
  N1: Disp1.pin1, R9.Pin_1
  N2: Disp1.pin2, R8.Pin_1
  N3: Disp1.pin_3, U1.Q6
  N4: Disp1.pin_4, U1.Q5
  N5: Disp1.pin_5, R7.Pin_1
  N6: Disp1.pin_6, U1.Q3
  N7: Disp1.pin_7, R6.Pin_1
  N8: Disp1.pin_8, R5.Pin_1
  N9: Disp1.pin_9, R4.Pin_0
  N10: Disp1.pin_10, U1.Q4
  N11: Disp1.pin_11, U1.Q2
  N12: Disp1.pin_12, R2.Pin_0
  N13: Disp1.pin_13, U1.Q7
  N14: Disp1.pin_14, R3.Pin_0
  N15: Disp1.pin_15, U1.Q1
  N16: Disp1.pin_16, U1.Q0
  GND: 元件1.D0/RX, U1.GND, U1.OE, U2.GND, U2.OE
  N17: 元件1.D2, U1.DS
  N18: 元件1.D3, U2.DS
  N19: 元件1.D4, U1.SH_CP, U2.SH_CP
  N20: 元件1.D5, U1.ST_CP, U2.ST_CP
  VCC: 元件1.5V, U1.MR, U1.VCC, U2.MR, U2.VCC
  N21: U2.Q1, R8.Pin_0
  N22: U2.Q2, R6.Pin_0
  N23: U2.Q3, R9.Pin_0
  N24: U2.Q4, R2.Pin_1
  N25: U2.Q5, R5.Pin_0
  N26: U2.Q6, R3.Pin_1
  N27: U2.Q7, R4.Pin_1
  N28: U2.Q0, R7.Pin_0
